# Fritzing sketch basil (saved by Fritzing 0.9.0b)
breadboards: 1

parts:
  Part1 = Photon
  T1 = LM35 Temperature Sensor [package="TO92 [THT]"]
  U1 = SWITCH_SPDT [package=kps-1290]

nets:
  N1: Part1.A0, T1.Vout
  N2: Part1.WKP, U1.P
  GND: Part1.GND, T1.GND, U1.O
  N3: Part1.VIN, T1.+Vs, U1.S
